// Digital circuit CPLD-MAIN.dig as structural Verilog
module CPLD_MAIN (
  input  C25,
  input  CPU_nCLK,
  input  CPU_RnW,
  input  [10:0] CPU_A,
  input  [7:0] DATA_I,
  input  DUMMY,
  output nIRQ_O,
  output [2:0] R_O,
  output [2:0] G_O,
  output [2:0] B_O,
  output HS_O,
  output VS_O,
  output [12:0] ADDR_O,
  output VRAM_nOE,
  output CPU_nCS0,
  output CPU_nCS1,
  output CPU_nCS2,
  output CPU_nCS3,
  output CPU_nOE,
  output CPU_nWE,
  output VRAM_nCS0,
  output VRAM_nCS1,
  output VRAM_nCS2,
  output VRAM_nCS3,
  output CPU_nWSE
);

  wire ACT, and_1_out, C25_8, d_ff_1_q, d_ff_2_q, IRQ, jk_ff_1_q, multiplexer_1_out, nC25_8, not_1_out;
  wire [1:0] DIV;
  wire [2:0] DIV_out;
  wire [7:0] D0_q, D1_q;
  wire [14:13] CNT_out;

  Counter #(.Bits(3)) u_DIV (.en(1'b1), .C(C25), .clr(1'b0), .out(DIV_out));  // open: ovf
  CPLD_SYNC cpld_sync_1 (.nC25_8(nC25_8), .C25_8(C25_8), .ACT(ACT), .nHS(HS_O), .nVS(VS_O), .IRQ_S(IRQ));
  D_FF #(.Bits(3)) DELAY (.D(DIV_out), .C(C25), .Q({C25_8, DIV}));  // open: nQ
  not not_1 (not_1_out, DIV_out[2]);
  not not_2 (nC25_8, C25_8);
  Register #(.Bits(8)) D0 (.D(DATA_I), .C(not_1_out), .en(ACT), .Q(D0_q));
  and and_1 (and_1_out, CPU_A[2], CPU_A[3], CPU_A[4], CPU_A[5], CPU_A[6], CPU_A[7], CPU_A[8], CPU_A[9], CPU_A[10]);
  Register #(.Bits(8)) D1 (.D(D0_q), .C(nC25_8), .en(ACT), .Q(D1_q));
  nand nand_1 (CPU_nCS0, ~CPU_A[0], ~CPU_A[1], and_1_out);  // NAnd
  nand nand_2 (CPU_nCS1, CPU_A[0], ~CPU_A[1], and_1_out);  // NAnd
  nand nand_3 (CPU_nCS2, ~CPU_A[0], CPU_A[1], and_1_out);  // NAnd
  nand nand_4 (CPU_nCS3, CPU_A[0], CPU_A[1], and_1_out);
  not not_3 (CPU_nWSE, and_1_out);
  or or_1 (CPU_nOE, ~CPU_RnW, CPU_nCLK);  // Or
  or or_2 (CPU_nWE, CPU_nCLK, CPU_RnW);
  JK_FF jk_ff_1 (.J(IRQ), .C(C25), .K(d_ff_2_q), .Q(jk_ff_1_q));  // open: nQ
  Multiplexer #(.Selector_Bits(3)) multiplexer_1 (
    .sel({C25_8, DIV}), .in_0(D1_q[7]), .in_1(D1_q[6]), .in_2(D1_q[5]), .in_3(D1_q[4]), .in_4(D1_q[3]),
    .in_5(D1_q[2]), .in_6(D1_q[1]), .in_7(D1_q[0]), .out(multiplexer_1_out));
  Counter #(.Bits(15)) CNT (.en(ACT), .C(C25_8), .clr(IRQ), .out({CNT_out, ADDR_O}));  // open: ovf
  D_FF d_ff_1 (.D(jk_ff_1_q), .C(CPU_nCLK), .Q(d_ff_1_q));  // open: nQ
  D_FF d_ff_2 (.D(d_ff_1_q), .C(CPU_nCLK), .Q(d_ff_2_q));  // open: nQ
  and and_2 (B_O[2], ACT, multiplexer_1_out);
  nand nand_5 (VRAM_nCS0, ~CNT_out[13], ~CNT_out[14]);  // NAnd
  nand nand_6 (VRAM_nCS1, CNT_out[13], ~CNT_out[14]);  // NAnd
  nand nand_7 (VRAM_nCS2, ~CNT_out[13], CNT_out[14]);  // NAnd
  nand nand_8 (VRAM_nCS3, CNT_out[13], CNT_out[14]);
  nor nor_1 (nIRQ_O, d_ff_1_q, d_ff_2_q);
  not not_4 (VRAM_nOE, ACT);
  VGA TESTING (.R({3{B_O[2]}}), .G({3{B_O[2]}}), .B({3{B_O[2]}}), .H(HS_O), .V(VS_O), .C(C25));

  assign B_O[1:0] = {2{B_O[2]}};
  assign G_O = {3{B_O[2]}};
  assign R_O = {3{B_O[2]}};

  // Other names for the same wires on the sheet: BO[2:0] = {3{B_O[2]}}; GO[2:0] = {3{B_O[2]}}; RO[2:0] = {3{B_O[2]}};
  //   DIV[2] = C25_8; nCC = CPU_nCLK; nHS = HS_O; nVS = VS_O

  // Notes on the sheet:
  //   C25: Hz: 2147483647
  //   nIRQ_O: Interrupt Output
  //   R_O: Red Output
  //   G_O: Green Output
  //   B_O: Blue Output
  //   HS_O: Horizontal Sync Output
  //   VS_O: Vertical Sync Output
  //   ADDR_O: Video Address output
  //   VRAM_nOE: VRAM Read
  //   CPU_nCLK: CPU Clock Input
  //   CPU_RnW: CPU Read/Write Input, default 1
  //   CPU_A: CPU Address Input
  //   bits 13-23
  //   DATA_I: VRAM Data input
  //   CPU_nCS0: CPU Side VRAM Chip Select 0
  //   CPU_nCS1: CPU Side VRAM Chip Select 1
  //   CPU_nCS2: CPU Side VRAM Chip Select 2
  //   CPU_nCS3: CPU Side VRAM Chip Select 3
  //   CPU_nOE: CPU Side VRAM Read
  //   CPU_nWE: CPU Side VRAM Write
  //   VRAM_nCS0: VRAM Chip Select 0
  //   VRAM_nCS1: VRAM Chip Select 1
  //   VRAM_nCS2: VRAM Chip Select 2
  //   VRAM_nCS3: VRAM Chip Select 3
  //   CPU_nWSE: CPU Side Wait State Enable
  //   DUMMY: Only needed for my own board,
  //   the updated PCB doesn't need this input anymore
endmodule
