// Digital circuit CPLD-SYNC.dig as structural Verilog
module CPLD_SYNC (
  input  nC25_8,
  input  C25_8,
  output ACT,
  output nHS,
  output nVS,
  output IRQ_S
);

  wire and_1_out, and_2_out, and_3_out, and_4_out, and_5_out, and_6_out, comparator_1_eq, comparator_1_gt,
       comparator_2_eq, comparator_2_gt;
  wire [6:0] X_out;
  wire [9:0] Y_out;

  Counter #(.Bits(7)) X (.en(1'b1), .C(nC25_8), .clr(and_3_out), .out(X_out));  // open: ovf
  Counter #(.Bits(10)) Y (.en(and_3_out), .C(nC25_8), .clr(and_6_out), .out(Y_out));  // open: ovf
  Comparator #(.Bits(7)) comparator_1 (
    .a(X_out), .b(7'b1001111), .gt(comparator_1_gt), .eq(comparator_1_eq));  // open: lt
  and and_1 (and_1_out, X_out[0], ~X_out[1], ~X_out[2], ~X_out[3], X_out[4], ~X_out[5], X_out[6]);  // And
  and and_2 (and_2_out, X_out[0], ~X_out[1], X_out[2], X_out[3], X_out[4], ~X_out[5], X_out[6]);  // And
  and and_3 (and_3_out, X_out[0], X_out[1], ~X_out[2], ~X_out[3], ~X_out[4], X_out[5], X_out[6]);  // And
  Comparator #(.Bits(10)) comparator_2 (
    .a(Y_out), .b(10'h18f), .gt(comparator_2_gt), .eq(comparator_2_eq));  // open: lt
  and and_4 (and_4_out, Y_out[0], ~Y_out[1], ~Y_out[2], ~Y_out[3], ~Y_out[4], ~Y_out[5], Y_out[6], Y_out[7], Y_out[8], ~Y_out[9]);  // And
  and and_5 (and_5_out, Y_out[0], Y_out[1], ~Y_out[2], ~Y_out[3], ~Y_out[4], ~Y_out[5], Y_out[6], Y_out[7], Y_out[8], ~Y_out[9]);  // And
  and and_6 (and_6_out, ~Y_out[0], ~Y_out[1], Y_out[2], Y_out[3], ~Y_out[4], ~Y_out[5], ~Y_out[6], ~Y_out[7], ~Y_out[8], Y_out[9], and_3_out);  // And
  JK_FF HSYNC (.J(and_1_out), .C(C25_8), .K(and_2_out), .nQ(nHS));  // open: Q
  JK_FF VSYNC (.J(and_4_out), .C(C25_8), .K(and_5_out), .nQ(nVS));  // open: Q
  nor nor_1 (ACT, comparator_2_gt, comparator_1_gt);
  and and_7 (IRQ_S, comparator_1_eq, comparator_2_eq);

  // Notes on the sheet:
  //   ACT: Active Area
  //   nHS: Horizontal Sync
  //   nVS: Vertical Sync
  //   IRQ_S: IRQ Output
  //   nC25_8: Hz: 2147483647
  //   C25_8: Hz: 2147483647
endmodule
